# Fritzing sketch bracelet (saved by Fritzing 0.9.2b)
breadboards: 1

parts:
  BAT1 = Battery Holders [package=battery-aaa]
  U3 = SWITCH-SPST-2 [package=switch-spst-vertical]
  LED2 = smd LED [color="Red (633nm)" package="1206 [SMD]"]
  R1 = Resistor [tolerance=±5% resistance=220 package="2010 [SMD]"]
  M1 = DC Motor
  M2 = DC Motor
  U1 = ESP8266 WiFi Module [part_number=ESP8266]
  D1 = Rectifier Diode [part_number=1N4001 package="300 mil [THT]"]
  R2 = Resistor [tolerance=±5% resistance=220 package=THT]
  Q2 = NPN-Transistor [package="TO92 [THT]"]
  D2 = Rectifier Diode [part_number=1N4001 package="300 mil [THT]"]
  R3 = Resistor [tolerance=±5% resistance=220 package=THT]
  Q3 = NPN-Transistor [package="TO92 [THT]"]

nets:
  N1: BAT1.-, LED2.cathode, U1.GND, Q2.C, Q3.C
  N2: BAT1.+, U3.O
  N3: U3.P, R1.Pin_0, M1.pin_1, M2.pin_1, U1.VCC, U1.CH_PD, D1.cathode, D2.cathode
  N4: LED2.anode, R1.Pin_1
  N5: M1.pin_2, D2.anode, Q3.E
  N6: M2.pin_2, D1.anode, Q2.E
  N7: U1.GPIO_0, R3.Pin_1
  N8: U1.GPIO_2, R2.Pin_1
  N9: R2.Pin_0, Q2.B
  N10: R3.Pin_0, Q3.B

custom parts:
  ESP8266 WiFi Module: Generic WiFi Module based on the ESP8266 with onboard PCB antenna and UART communications
